// Logisim project CPU.circ as structural Verilog: 5 circuits, main circuit ULA
module ULA (
  input  [15:0] A,
  input  [15:0] B,
  input  [3:0] op,
  output [15:0] out_4,
  output out_5
);

  wire OutBg, OutEq;
  wire [15:0] OutDiv, OutE, OutNot, OutOr, OutSub, OutSum, OutTimes;

  assign OutE = A & B;  // AND_Gate and_1, 16 bits wide
  assign OutOr = A | B;  // OR_Gate or_1, 16 bits wide
  assign OutNot = ~A;  // NOT_Gate not_1, 16 bits wide
  Adder #(.width(16)) adder_1 (.a(A), .b(B), .out(OutSum));  // open: cin, cout
  Multiplier #(.width(16)) multiplier_1 (.a(A), .b(B), .out(OutTimes));  // open: cin, cout
  Subtractor #(.width(16)) subtractor_1 (.a(A), .b(B), .out(OutSub));  // open: bin, bout
  Divider #(.width(16)) divider_1 (.a(A), .b(B), .out(OutDiv));  // open: upper, rem
  Comparator #(.width(16)) comparator_1 (.a(A), .b(B), .gt(OutBg), .eq(OutEq));  // open: lt
  Multiplexer #(.select(4), .width(16), .enable("false")) multiplexer_1 (
    .in0(OutSum), .in1(OutTimes), .in2(OutSub), .in3(OutDiv), .in4(OutE), .in5(OutOr), .in6(OutNot),
    .in14({16{1'b0}}), .in15({16{1'b0}}), .out(out_4), .sel(op));  // open: in7, in8, in9, in10, in11, in12, in13
  Multiplexer #(.select(4), .enable("false")) multiplexer_2 (
    .in14(OutBg), .in15(OutEq), .out(out_5), .sel(op));  // open: in0, in1, in2, in3, in4, in5, in6, in7, in8, in9, in10, in11, in12, in13
endmodule

module Main (
);

  ROM #(.addrWidth(12), .dataWidth(16)) rom_1 ();  // open: addr, data, sel
  RAM #(.addrWidth(12), .dataWidth(16), .bus("separate")) ram_1 ();  // open: addr, din, data, str, sel, clk, ld, clr
endmodule

module MEMLec (
  input  in_1,
  input  in_2,
  input  in_3,
  input  in_4,
  input  in_5,
  input  in_6,
  input  in_7,
  input  in_8,
  input  in_9,
  input  in_10,
  input  in_11,
  input  in_12,
  input  [7:0] in_13,
  input  in_14,
  input  in_15,
  output out_16,
  output out_17,
  output out_18,
  output out_19,
  output out_20,
  output out_21,
  output [7:0] out_22
);

  wire and_1_out, and_2_out, and_3_out, and_4_out, and_5_out, and_6_out, and_7_out, and_8_out, and_9_out,
       and_10_out, and_11_out, and_12_out, and_13_out, and_14_out, and_15_out, and_16_out, and_17_out,
       and_18_out, and_19_out, and_20_out, clock_1_out, clock_2_out, clock_3_out, clock_4_out, clock_5_out,
       not_1_out, not_2_out, not_3_out, not_4_out, not_5_out, not_6_out, not_8_out, not_9_out, not_10_out,
       not_11_out, not_13_out, not_14_out, not_15_out, not_16_out, not_17_out, not_19_out, not_20_out,
       not_21_out, not_23_out;

  Clock clock_1 (.out(clock_1_out));
  Clock clock_2 (.out(clock_2_out));
  not not_1 (not_1_out, in_2);
  and and_1 (and_1_out, not_1_out, not_8_out);
  and and_2 (and_2_out, out_17, not_2_out);
  not not_2 (not_2_out, in_3);
  and and_3 (and_3_out, in_4, clock_1_out);
  not not_3 (not_3_out, and_3_out);
  not not_4 (not_4_out, and_4_out);
  and and_4 (and_4_out, clock_1_out, in_5);
  Clock clock_3 (.out(clock_3_out));
  not not_5 (not_5_out, in_6);
  Clock clock_4 (.out(clock_4_out));
  and and_5 (and_5_out, clock_4_out, in_9);
  not not_6 (not_6_out, in_8);
  D_Flip_Flop d_ff_1 (.clk(clock_2_out), .D(in_10), .Q(out_21), .en(in_11), .reset(in_12));  // open: Qn, preset
  Clock clock_5 (.out(clock_5_out));
  not not_7 (out_17, and_1_out);
  not not_8 (not_8_out, and_2_out);
  and and_6 (and_6_out, not_3_out, not_13_out);
  and and_7 (and_7_out, out_18, not_4_out);
  and and_8 (and_8_out, in_6, and_9_out);
  and and_9 (and_9_out, clock_3_out, in_7);
  and and_10 (and_10_out, and_9_out, not_5_out);
  not not_9 (not_9_out, clock_4_out);
  and and_11 (and_11_out, in_8, and_5_out);
  not not_10 (not_10_out, and_11_out);
  and and_12 (and_12_out, and_5_out, not_6_out);
  not not_11 (not_11_out, and_12_out);
  Register register_1 (.D(in_13), .en(in_14), .Q(out_22), .clk(clock_5_out), .clr(in_15));
  not not_12 (out_18, and_6_out);
  not not_13 (not_13_out, and_7_out);
  not not_14 (not_14_out, and_8_out);
  and and_13 (and_13_out, not_14_out, not_19_out);
  and and_14 (and_14_out, out_19, not_15_out);
  not not_15 (not_15_out, and_10_out);
  not not_16 (not_16_out, and_15_out);
  and and_15 (and_15_out, not_10_out, not_17_out);
  not not_17 (not_17_out, and_16_out);
  and and_16 (and_16_out, not_16_out, not_11_out);
  not not_18 (out_19, and_13_out);
  not not_19 (not_19_out, and_14_out);
  and and_17 (and_17_out, not_9_out, not_16_out);
  and and_18 (and_18_out, not_9_out, not_17_out);
  not not_20 (not_20_out, and_17_out);
  and and_19 (and_19_out, not_20_out, not_23_out);
  and and_20 (and_20_out, out_20, not_21_out);
  not not_21 (not_21_out, and_18_out);
  not not_22 (out_20, and_19_out);
  not not_23 (not_23_out, and_20_out);

  assign out_16 = in_1;
endmodule

module MEM (
  input  [15:0] in_1,
  input  [3:0] in_2,
  input  [3:0] in_3,
  input  in_4,
  input  Clock,
  input  Enable,
  output [15:0] out_7,
  output [15:0] out_8
);

  wire E0, E1, E2, E3, E4, E5, E6, E7, MC;
  wire [15:0] S0, S1, S2, S3, S4, S5, S6, S7;

  and and_1 (MC, Clock, Enable);
  Multiplexer #(.select(4), .width(16)) multiplexer_1 (
    .in0(S0), .in1(S1), .in2(S2), .in3(S3), .in4(S4), .in5(S5), .in6(S6), .in7(S7), .out(out_7), .sel(in_2));  // open: in8, in9, in10, in11, in12, in13, in14, in15, en
  Register #(.width(16)) register_1 (.D(in_1), .en(E0), .Q(S0), .clk(MC), .clr(in_4));
  Register #(.width(16)) register_2 (.D(in_1), .en(E2), .Q(S2), .clk(MC), .clr(in_4));
  Register #(.width(16)) register_3 (.D(in_1), .en(E4), .Q(S4), .clk(MC), .clr(in_4));
  Register #(.width(16)) register_4 (.D(in_1), .en(E6), .Q(S6), .clk(MC), .clr(in_4));
  Multiplexer #(.select(4), .width(16)) multiplexer_2 (
    .in0(S0), .in1(S1), .in2(S2), .in3(S3), .in4(S4), .in5(S5), .in6(S6), .in7(S7), .out(out_8), .sel(in_3));  // open: in8, in9, in10, in11, in12, in13, in14, in15, en
  Register #(.width(16)) register_5 (.D(in_1), .en(E1), .Q(S1), .clk(MC), .clr(in_4));
  Register #(.width(16)) register_6 (.D(in_1), .en(E3), .Q(S3), .clk(MC), .clr(in_4));
  Register #(.width(16)) register_7 (.D(in_1), .en(E5), .Q(S5), .clk(MC), .clr(in_4));
  Register #(.width(16)) register_8 (.D(in_1), .en(E7), .Q(S7), .clk(MC), .clr(in_4));
  Demultiplexer #(.select(4)) demultiplexer_1 (
    .out0(E0), .out1(E1), .out2(E2), .out3(E3), .out4(E4), .out5(E5), .out6(E6), .out7(E7), .in(1'b1),
    .sel(in_2));  // open: out8, out9, out10, out11, out12, out13, out14, out15, en

  // Other names for the same wires on the sheet: AddA[3:0] = in_2; AddB[3:0] = in_3; Data[15:0] = in_1;
  //   OutA[15:0] = out_7; OutB[15:0] = out_8; Reset = in_4
endmodule

module CPU (
  input  [3:0] in_1,
  input  [3:0] in_2,
  input  in_3,
  input  in_4,
  input  [3:0] in_5,
  input  [7:0] in_6,
  input  [7:0] in_7
);

  wire clock_1_out;
  wire [15:0] mem_1_out_7, mem_1_out_8, multiplexer_1_out, ula_1_out_4;

  Clock clock_1 (.out(clock_1_out));
  // Probe on mem_1_out_7
  MEM mem_1 (
    .in_1(multiplexer_1_out), .in_2(in_1), .in_3(in_2), .in_4(in_4), .Clock(clock_1_out), .Enable(in_3),
    .out_7(mem_1_out_7), .out_8(mem_1_out_8));
  ULA ula_1 (.A(mem_1_out_7), .B(mem_1_out_8), .op(in_5), .out_4(ula_1_out_4));  // open: out_5
  Multiplexer #(.select(2), .width(16)) multiplexer_1 (
    .in0(ula_1_out_4), .in1({{8{1'b0}}, in_6}), .in2({in_7, {8{1'b0}}}), .out(multiplexer_1_out));  // open: in3, sel, en
endmodule
